// Logisim project CPU.circ as structural Verilog: 6 circuits, main circuit main
module main (
  input  [7:0] in_1,
  input  in_2,
  input  in_3,
  output [7:0] out_4
);

  _8Register u_8register_1 (.in_1(in_1), .in_2(in_2), .in_3(in_3), .out_4(out_4));
endmodule

module _1M (
  input  in_1,
  input  in_2,
  output out_3
);

  wire nand_1_out, nand_2_out, nand_4_out;

  nand nand_1 (nand_1_out, in_1, in_2);
  nand nand_2 (nand_2_out, nand_1_out, in_2);
  nand nand_3 (out_3, nand_1_out, nand_4_out);
  nand nand_4 (nand_4_out, out_3, nand_2_out);
endmodule

module _8M (
  input  [7:0] in_1,
  input  in_2,
  output [7:0] out_3
);

  _1M u_1m_1 (.in_1(in_1[0]), .in_2(in_2), .out_3(out_3[0]));
  _1M u_1m_2 (.in_1(in_1[1]), .in_2(in_2), .out_3(out_3[1]));
  _1M u_1m_3 (.in_1(in_1[2]), .in_2(in_2), .out_3(out_3[2]));
  _1M u_1m_4 (.in_1(in_1[3]), .in_2(in_2), .out_3(out_3[3]));
  _1M u_1m_5 (.in_1(in_1[4]), .in_2(in_2), .out_3(out_3[4]));
  _1M u_1m_6 (.in_1(in_1[5]), .in_2(in_2), .out_3(out_3[5]));
  _1M u_1m_7 (.in_1(in_1[6]), .in_2(in_2), .out_3(out_3[6]));
  _1M u_1m_8 (.in_1(in_1[7]), .in_2(in_2), .out_3(out_3[7]));
endmodule

module _8Register (
  input  [7:0] in_1,
  input  in_2,
  input  in_3,
  output [7:0] out_4
);

  wire [7:0] n8m_1_out_3;

  _8M u_8m_1 (.in_1(in_1), .in_2(in_2), .out_3(n8m_1_out_3));
  Enabler enabler_1 (.in_1(n8m_1_out_3), .in_2(in_3), .out_3(out_4));
endmodule

module Enabler (
  input  [7:0] in_1,
  input  in_2,
  output [7:0] out_3
);

  and and_1 (out_3[0], in_1[0], in_2);
  and and_2 (out_3[1], in_1[1], in_2);
  and and_3 (out_3[2], in_1[2], in_2);
  and and_4 (out_3[3], in_1[3], in_2);
  and and_5 (out_3[4], in_1[4], in_2);
  and and_6 (out_3[5], in_1[5], in_2);
  and and_7 (out_3[6], in_1[6], in_2);
  and and_8 (out_3[7], in_1[7], in_2);
endmodule

module BUS (
  input  [7:0] in_1,
  input  in_2,
  input  in_3,
  input  in_4,
  input  in_5,
  output [7:0] out_6,
  output [7:0] out_7
);

  wire nor_1_out;
  wire [7:0] controlled_buffer_1_out;

  assign controlled_buffer_1_out = nor_1_out ? in_1 : 8'bz;  // Controlled_Buffer controlled_buffer_1
  nor nor_1 (nor_1_out, in_3, in_5);
  assign controlled_buffer_1_out = in_3 ? out_6 : 8'bz;  // Controlled_Buffer controlled_buffer_2
  _8Register u_8register_1 (.in_1(controlled_buffer_1_out), .in_2(in_2), .in_3(in_3), .out_4(out_6));
  assign controlled_buffer_1_out = in_5 ? out_7 : 8'bz;  // Controlled_Buffer controlled_buffer_3
  _8Register u_8register_2 (.in_1(controlled_buffer_1_out), .in_2(in_4), .in_3(in_5), .out_4(out_7));
endmodule
